# Fritzing sketch bursting_bubbles (saved by Fritzing 0.7.12b)
breadboards: 1

parts:
  3_3V = LiPoly Battery (1300mAh)
  Arduino_Mini_Pro = Arduino Pro Mini 3.3V
  XBee_WiFly = XBee
  Q1 = Basic FET N-Channel [package="TO220 [THT]"]
  R1 = 1k Ω Resistor [package=THT]
  VCC1 = Battery
  M1 = DC Motor

nets:
  VCC: 3_3V.positive, Arduino_Mini_Pro.VCC, XBee_WiFly.VCC
  GND: 3_3V.negative, Arduino_Mini_Pro.GND, XBee_WiFly.GND, Q1.source, VCC1.-, M1.pin_1
  N1: Arduino_Mini_Pro.D4, R1.Pin_1
  N2: Arduino_Mini_Pro.RXI, XBee_WiFly.pin2
  N3: Arduino_Mini_Pro.TXO, XBee_WiFly.pin3
  N4: Q1.gate, R1.Pin_0
  N5: Q1.drain, VCC1.+, M1.pin_2

notes:
  makingthingshappen.de
  burstin bubbles
  CC BY-SA 3.0 Sven Kräuter
  kit

custom parts:
  LiPoly Battery (1300mAh): Lithium Ion Polymer Battery (1300mAh)
