# Fritzing sketch bursting_bubbles_yun (saved by Fritzing 0.7.12b)
breadboards: 1

parts:
  Q1 = Basic FET N-Channel [package="TO220 [THT]"]
  R1 = 1k Ω Resistor [package=THT]
  VCC1 = Battery
  M1 = DC Motor
  Arduino_Yun = Arduino

nets:
  N1: Q1.gate, R1.Pin_0
  N2: Q1.drain, VCC1.+, M1.pin_2
  N3: Q1.source, VCC1.-, M1.pin_1, Arduino_Yun.GND
  N4: R1.Pin_1, Arduino_Yun.D4

notes:
  makingthingshappen.de
  burstin bubbles
  CC BY-SA 3.0 Sven Kräuter
  kit
